// Logisim project 22_8_19.circ as structural Verilog: 1 circuit, main circuit main
module main (
  input  in_1,
  input  in_2,
  input  in_3,
  input  in_4,
  input  in_5,
  input  in_6,
  input  in_7,
  input  in_8,
  input  in_9,
  input  in_10,
  input  in_11,
  input  in_12,
  input  in_13,
  input  in_14,
  input  in_15,
  output out_16,
  output out_17,
  output out_18,
  output out_19,
  output out_20,
  output out_21,
  output out_22
);

  wire nor_1_out, nor_2_out, nor_3_out, not_1_out, not_2_out, not_3_out, not_4_out, not_5_out, not_6_out,
       not_7_out, not_8_out, not_9_out, not_10_out, or_1_out, or_2_out, or_3_out;

  not not_1 (not_1_out, in_6);
  not not_2 (not_2_out, in_11);
  xor xor_1 (out_17, in_2, in_1);
  not not_3 (not_3_out, in_7);
  not not_4 (not_4_out, in_12);
  not not_5 (not_5_out, in_8);
  not not_6 (not_6_out, in_13);
  xor xor_2 (out_18, in_3, in_2);
  not not_7 (not_7_out, in_9);
  not not_8 (not_8_out, in_14);
  not not_9 (not_9_out, in_10);
  not not_10 (not_10_out, in_15);
  xor xor_3 (out_19, in_4, in_3);
  or or_1 (or_1_out, in_7, in_9);
  or or_2 (or_2_out, not_3_out, not_7_out, in_10);
  or or_3 (or_3_out, not_1_out, not_3_out, not_7_out);
  nor nor_1 (nor_1_out, in_12, in_14);
  nor nor_2 (nor_2_out, not_4_out, not_8_out, in_15);
  nor nor_3 (nor_3_out, not_2_out, not_4_out, not_8_out);
  xor xor_4 (out_20, in_5, in_4);
  and and_1 (out_21, or_1_out, or_2_out, or_3_out);
  nor nor_4 (out_22, nor_1_out, nor_2_out, nor_3_out);

  assign out_16 = in_1;

  // Notes on the sheet:
  //   Binary to Gray Code
endmodule
