// Logisim project Logic Gate.circ as structural Verilog: 1 circuit, main circuit main
module main (
  input  in_1,
  input  in_2,
  input  in_3,
  input  in_4,
  input  in_5,
  input  in_6,
  input  in_7,
  input  in_8,
  input  in_9,
  input  in_10,
  output out_11,
  output out_12,
  output out_13,
  output out_14,
  output out_15,
  output out_16
);

  wire nand_1_out, nand_3_out, nand_4_out, nand_5_out, nand_6_out, nor_1_out, nor_2_out, nor_3_out,
       nor_4_out, nor_5_out, nor_7_out, nor_8_out;

  nor nor_1 (nor_1_out, in_1, in_1);
  nor nor_2 (nor_2_out, in_2, in_2);
  nand nand_1 (nand_1_out, in_10, in_10);
  nor nor_3 (nor_3_out, in_2, nor_1_out);
  nor nor_4 (nor_4_out, in_1, nor_2_out);
  nand nand_2 (out_13, in_4, in_4);
  nand nand_3 (nand_3_out, in_6, in_7);
  nand nand_4 (nand_4_out, in_9, in_9);
  nand nand_5 (nand_5_out, nand_1_out, in_9);
  nor nor_5 (nor_5_out, nor_3_out, nor_4_out);
  nand nand_6 (nand_6_out, nand_4_out, in_10);
  nand nand_7 (out_14, nand_3_out, nand_3_out);
  nand nand_8 (out_16, nand_6_out, nand_5_out);
  nor nor_6 (out_11, nor_5_out, nor_5_out);
  nor nor_7 (nor_7_out, in_5, in_5);
  nor nor_8 (nor_8_out, in_8, in_8);
  nor nor_9 (out_12, in_3, in_3);
  nor nor_10 (out_15, nor_7_out, nor_8_out);

  // Notes on the sheet:
  //   XOR using NOR
  //   NOT using NAND
  //   AND using NAND
  //   XOR using NAND
  //   NOT using NOR
  //   AND using NOR
endmodule
