// Logisim project flipflop.circ as structural Verilog: 1 circuit, main circuit main
module main (
  input  in_1,
  input  in_2,
  input  in_3,
  input  in_4,
  input  in_5,
  input  in_6,
  input  in_7,
  input  in_8,
  output out_9,
  output out_10,
  output out_11,
  output out_12,
  output out_13,
  output out_14,
  output out_15,
  output out_16,
  output out_17,
  output out_18
);

  wire clock_1_out, clock_2_out, clock_3_out, clock_4_out, clock_5_out, nand_1_out, nand_2_out, nand_3_out,
       nand_4_out, nand_5_out, nand_6_out, nand_7_out, nand_8_out, nand_9_out, nand_10_out, nand_11_out,
       nand_12_out, nand_21_out, nand_22_out, not_1_out, not_2_out;

  Clock clock_1 (.out(clock_1_out));
  Clock clock_2 (.out(clock_2_out));
  not not_1 (not_1_out, in_5);
  Clock clock_3 (.out(clock_3_out));
  Clock clock_4 (.out(clock_4_out));
  nand nand_1 (nand_1_out, in_7, out_18, clock_1_out);
  nand nand_2 (nand_2_out, clock_1_out, out_17, in_8);
  nand nand_3 (nand_3_out, clock_2_out, in_2);
  Clock clock_5 (.out(clock_5_out));
  nand nand_4 (nand_4_out, clock_3_out, not_1_out);
  nand nand_5 (nand_5_out, in_1, clock_2_out);
  nand nand_6 (nand_6_out, in_3, out_12, clock_5_out);
  nand nand_7 (nand_7_out, clock_5_out, out_11, in_4);
  nand nand_8 (nand_8_out, in_5, clock_3_out);
  nand nand_9 (nand_9_out, in_6, out_16, clock_4_out);
  nand nand_10 (nand_10_out, clock_4_out, out_15, in_6);
  nand nand_11 (nand_11_out, nand_1_out, nand_12_out);
  nand nand_12 (nand_12_out, nand_11_out, nand_2_out);
  not not_2 (not_2_out, clock_1_out);
  nand nand_13 (out_9, nand_5_out, out_10);
  nand nand_14 (out_10, out_9, nand_3_out);
  nand nand_15 (out_11, nand_6_out, out_12);
  nand nand_16 (out_12, out_11, nand_7_out);
  nand nand_17 (out_13, nand_8_out, out_14);
  nand nand_18 (out_14, out_13, nand_4_out);
  nand nand_19 (out_15, nand_9_out, out_16);
  nand nand_20 (out_16, out_15, nand_10_out);
  nand nand_21 (nand_21_out, nand_11_out, not_2_out);
  nand nand_22 (nand_22_out, not_2_out, nand_12_out);
  nand nand_23 (out_17, nand_21_out, out_18);
  nand nand_24 (out_18, out_17, nand_22_out);

  // Notes on the sheet:
  //   SR Flip Flop
  //   JK Flip Flop
  //   D Flip Flop
  //   T Flip Flop
  //   Master Slave
endmodule
