// Logisim project flipflopconversion.circ as structural Verilog: 1 circuit, main circuit main
module main (
  input  in_1,
  input  in_2,
  input  in_3,
  output out_4,
  output out_5,
  output out_6,
  output out_7
);

  wire and_1_out, and_2_out, clock_1_out, clock_2_out, not_1_out;

  Clock clock_1 (.out(clock_1_out));
  and and_1 (and_1_out, out_5, in_1);
  and and_2 (and_2_out, in_2, out_4);
  Clock clock_2 (.out(clock_2_out));
  not not_1 (not_1_out, in_3);
  S_R_Flip_Flop s_r_ff_1 (
    .S(and_1_out), .clk(clock_1_out), .R(and_2_out), .Q(out_4), .Qn(out_5));  // open: preset, reset, en
  S_R_Flip_Flop s_r_ff_2 (
    .S(in_3), .clk(clock_2_out), .R(not_1_out), .Q(out_6), .Qn(out_7));  // open: preset, reset, en

  // Notes on the sheet:
  //   SR to JK Flip Flop
  //   SR to D Flip Flop
endmodule
