// Logisim project 4bitlookahead_hextobinencoder_2bit3bitadder.circ as structural Verilog: 1 circuit, main circuit main
module main (
  input  in_1,
  input  in_2,
  input  in_3,
  input  in_4,
  input  in_5,
  input  in_6,
  input  in_7,
  input  in_8,
  input  in_9,
  input  in_10,
  input  in_11,
  input  in_12,
  input  in_13,
  input  in_14,
  input  in_15,
  input  in_16,
  input  in_17,
  input  in_18,
  input  in_19,
  input  in_20,
  input  in_21,
  input  in_22,
  input  in_23,
  input  in_24,
  input  in_25,
  input  in_26,
  input  in_27,
  input  in_28,
  input  in_29,
  input  in_30,
  output out_31,
  output out_32,
  output out_33,
  output out_34,
  output out_35,
  output out_36,
  output out_37,
  output out_38,
  output out_39,
  output out_40,
  output out_41,
  output out_42,
  output out_43
);

  wire adder_1_cout, adder_2_cout, adder_3_cout, and_1_out, and_2_out, and_3_out, and_4_out, and_5_out,
       and_6_out, and_7_out, and_8_out, and_9_out, and_10_out, and_11_out, and_12_out, and_13_out,
       and_14_out, and_15_out, and_16_out, and_17_out, and_18_out, not_1_out, not_2_out, not_3_out,
       not_4_out, not_5_out;

  not not_1 (not_1_out, in_26);
  not not_2 (not_2_out, in_27);
  not not_3 (not_3_out, in_28);
  not not_4 (not_4_out, in_29);
  not not_5 (not_5_out, in_30);
  Adder #(.width(1)) adder_1 (.a(in_2), .b(in_3), .out(out_31), .cin(in_1), .cout(adder_1_cout));
  Adder #(.width(1)) adder_2 (.a(in_4), .b(in_5), .out(out_32), .cin(adder_1_cout), .cout(adder_2_cout));
  Adder #(.width(1)) adder_3 (.a(in_6), .b(in_7), .out(out_33), .cin(adder_2_cout), .cout(adder_3_cout));
  Adder #(.width(1)) adder_4 (.a(in_8), .b(in_9), .out(out_34), .cin(adder_3_cout), .cout(out_35));
  and and_1 (and_1_out, in_26, in_27, in_28, in_29);
  and and_2 (and_2_out, in_26, in_27, in_28, in_30);
  and and_3 (and_3_out, in_27, in_28, in_29, in_30);
  and and_4 (and_4_out, in_26, not_3_out, in_29);
  and and_5 (and_5_out, in_27, not_3_out, in_29, in_30);
  and and_6 (and_6_out, in_26, in_27, not_3_out, in_30);
  and and_7 (and_7_out, not_1_out, not_2_out, in_28);
  and and_8 (and_8_out, not_2_out, in_28, not_4_out);
  and and_9 (and_9_out, not_1_out, in_27, in_28, in_30);
  and and_10 (and_10_out, not_1_out, in_28, in_29, not_5_out);
  and and_11 (and_11_out, not_1_out, in_29, not_5_out);
  and and_12 (and_12_out, in_26, not_4_out, not_5_out);
  and and_13 (and_13_out, in_26, not_2_out, not_4_out);
  and and_14 (and_14_out, not_1_out, not_2_out, in_29);
  and and_15 (and_15_out, not_1_out, in_27, not_4_out, in_30);
  and and_16 (and_16_out, in_26, in_27, in_29, in_30);
  and and_17 (and_17_out, in_26, not_2_out);
  and and_18 (and_18_out, in_27, not_5_out);
  or or_1 (out_36, in_18, in_19, in_20, in_21, in_22, in_23, in_24, in_25);
  or or_2 (out_37, in_14, in_15, in_16, in_17, in_22, in_23, in_24, in_25);
  or or_3 (out_38, in_12, in_13, in_16, in_17, in_20, in_21, in_24, in_25);
  or or_4 (out_39, in_11, in_13, in_15, in_17, in_19, in_21, in_23, in_25);
  or or_5 (out_40, and_1_out, and_2_out, and_3_out);
  or or_6 (out_41, and_4_out, and_5_out, and_6_out, and_7_out, and_8_out, and_9_out, and_10_out);
  or or_7 (out_42, and_11_out, and_12_out, and_13_out, and_14_out, and_15_out, and_16_out);
  or or_8 (out_43, and_17_out, and_18_out);

  // Notes on the sheet:
  //   0      1      2      3      4      5     6     7     8      9     A     B     C     D     E     F
  //   Hexadecimal to binary encoder
  //   2 bit and 3bit adder
  //   4 bit look ahead carry adder
endmodule
