// Logisim project decoder-fulladder-fullsubtracter.circ as structural Verilog: 1 circuit, main circuit main
module main (
  input  in_1,
  input  [2:0] in_2,
  input  in_3,
  input  [2:0] in_4,
  input  in_5,
  input  [2:0] in_6,
  input  in_7,
  input  in_8,
  input  in_9,
  input  in_10,
  input  in_11,
  input  in_12,
  input  in_13,
  input  in_14,
  input  in_15,
  input  in_16,
  input  in_17,
  output out_18,
  output out_19,
  output out_20,
  output out_21,
  output out_22,
  output out_23,
  output out_24,
  output out_25,
  output out_26,
  output out_27,
  output out_28,
  output out_29,
  output out_30,
  output out_31,
  output out_32,
  output out_33,
  output out_34,
  output out_35,
  output out_36,
  output out_37,
  output out_38,
  output out_39,
  output out_40,
  output out_41,
  output out_42,
  output out_43,
  output out_44,
  output out_45,
  output out_46,
  output out_47,
  output out_48,
  output out_49,
  output out_50,
  output out_51,
  output out_52,
  output out_53,
  output out_54,
  output out_55
);

  wire and_1_out, and_2_out, and_3_out, and_4_out, and_5_out, and_6_out, and_7_out, and_8_out, and_9_out,
       and_10_out, and_11_out, and_12_out, and_13_out, and_14_out, and_15_out, and_16_out, and_17_out,
       and_18_out, and_19_out, and_20_out, decoder_5_out2, decoder_5_out3, decoder_5_out4, decoder_5_out5,
       decoder_5_out6, decoder_5_out7, not_1_out, not_2_out, not_3_out, not_4_out, not_5_out, not_6_out,
       not_7_out, not_8_out, or_1_out, or_2_out, or_3_out, or_4_out, or_5_out, or_6_out, or_7_out, xor_1_out,
       xor_2_out;

  not not_1 (not_1_out, in_7);
  not not_2 (not_2_out, in_8);
  not not_3 (not_3_out, in_5);
  not not_4 (not_4_out, in_9);
  not not_5 (not_5_out, in_15);
  Decoder #(.select(3)) decoder_1 (
    .out0(out_18), .out1(out_19), .out2(out_20), .out3(out_22), .out4(out_24), .out5(out_26), .out6(out_28),
    .out7(out_30), .sel(in_2), .en(in_1));
  Decoder #(.select(3)) decoder_2 (
    .out0(out_34), .out1(out_36), .out2(out_38), .out3(out_39), .out4(out_40), .out5(out_41), .out6(out_42),
    .out7(out_43), .sel(in_6), .en(not_3_out));
  Decoder #(.select(3)) decoder_3 (
    .out0(out_44), .out1(out_45), .out2(out_46), .out3(out_47), .out4(out_48), .out5(out_49), .out6(out_50),
    .out7(out_51), .sel(in_6), .en(in_5));
  not not_6 (not_6_out, in_10);
  xor xor_1 (xor_1_out, in_12, in_13);
  and and_1 (and_1_out, in_12, in_13);
  xor xor_2 (xor_2_out, in_15, in_16);
  and and_2 (and_2_out, not_5_out, in_16);
  and and_3 (and_3_out, in_8, in_10);
  and and_4 (and_4_out, not_6_out, not_2_out);
  and and_5 (and_5_out, not_4_out, not_6_out);
  and and_6 (and_6_out, in_9, in_10);
  and and_7 (and_7_out, not_2_out, not_6_out);
  and and_8 (and_8_out, in_8, not_4_out, in_10);
  and and_9 (and_9_out, in_9, not_6_out);
  and and_10 (and_10_out, in_9, not_2_out);
  and and_11 (and_11_out, not_2_out, not_6_out);
  and and_12 (and_12_out, in_9, not_6_out);
  and and_13 (and_13_out, not_4_out, not_6_out);
  and and_14 (and_14_out, in_8, not_6_out);
  and and_15 (and_15_out, in_8, not_4_out);
  and and_16 (and_16_out, in_8, not_4_out);
  and and_17 (and_17_out, in_9, not_6_out);
  and and_18 (and_18_out, not_2_out, in_9);
  or or_1 (or_1_out, and_11_out, and_12_out);
  not not_7 (not_7_out, xor_2_out);
  or or_2 (or_2_out, in_7, in_9, and_3_out, and_4_out);
  or or_3 (or_3_out, and_5_out, and_6_out, not_2_out);
  or or_4 (or_4_out, in_8, not_4_out, in_10);
  or or_5 (or_5_out, and_7_out, and_8_out, and_10_out, and_9_out, in_7);
  or or_6 (or_6_out, and_13_out, and_14_out, in_7, and_15_out);
  or or_7 (or_7_out, and_16_out, and_17_out, and_18_out, in_7);
  xor xor_3 (out_52, xor_1_out, in_14);
  and and_19 (and_19_out, xor_1_out, in_14);
  xor xor_4 (out_54, xor_2_out, in_17);
  and and_20 (and_20_out, not_7_out, in_17);
  or or_8 (out_53, and_19_out, and_1_out);
  or or_9 (out_55, and_20_out, and_2_out);
  _7_Segment_Display u_7_segment_display_1 (
    .g(or_7_out), .f(or_6_out), .a(or_2_out), .b(or_3_out), .e(or_1_out), .d(or_5_out), .c(or_4_out),
    .dp(in_11));
  not not_8 (not_8_out, in_3);
  Decoder #(.select(3)) decoder_4 (
    .out0(out_21), .out1(out_23), .out2(out_25), .out3(out_27), .out4(out_29), .out5(out_31), .out6(out_32),
    .out7(out_33), .sel(in_4), .en(not_8_out));
  Decoder #(.select(3)) decoder_5 (
    .out0(out_35), .out1(out_37), .out2(decoder_5_out2), .out3(decoder_5_out3), .out4(decoder_5_out4),
    .out5(decoder_5_out5), .out6(decoder_5_out6), .out7(decoder_5_out7), .sel(in_4), .en(in_3));
  // also tied to GND on the sheet: {decoder_5_out3, decoder_5_out4, decoder_5_out5, decoder_5_out6, decoder_5_out7, decoder_5_out2}

  // Notes on the sheet:
  //   Binary to Octal using 3:8 decoder
  //   Binary to Hexa-Decimal using 3:8 decoder
  //   Full Adder
  //   Full Subracter
  //   7 segment display
  //   Binary to BCD using 3:8 decoder
endmodule
