// Logisim project register.circ as structural Verilog: 1 circuit, main circuit main
module main (
  input  in_1,
  input  in_2,
  input  in_3,
  input  in_4,
  input  in_5,
  input  in_6,
  input  in_7,
  input  in_8,
  input  in_9,
  input  in_10,
  output out_11,
  output out_12,
  output out_13,
  output out_14,
  output out_15,
  output out_16,
  output out_17,
  output out_18,
  output out_19,
  output out_20
);

  wire clock_1_out, clock_2_out, clock_3_out, clock_4_out, d_ff_2_q, d_ff_4_q, d_ff_6_q, d_ff_8_q, d_ff_10_q,
       d_ff_14_q, multiplexer_1_out, multiplexer_2_out, multiplexer_3_out;

  Clock clock_1 (.out(clock_1_out));
  Clock clock_2 (.out(clock_2_out));
  Clock clock_3 (.out(clock_3_out));
  Clock clock_4 (.out(clock_4_out));
  D_Flip_Flop d_ff_1 (.clk(clock_1_out), .D(in_3), .Q(out_16));  // open: Qn, preset, en, reset
  D_Flip_Flop d_ff_2 (.clk(clock_2_out), .D(in_7), .Q(d_ff_2_q));  // open: Qn, preset, en, reset
  D_Flip_Flop d_ff_3 (.clk(clock_3_out), .D(in_1), .Q(out_11));  // open: Qn, preset, en, reset
  D_Flip_Flop d_ff_4 (.clk(clock_4_out), .D(in_2), .Q(d_ff_4_q));  // open: Qn, preset, en, reset
  Multiplexer multiplexer_1 (.in0(d_ff_2_q), .in1(in_8), .out(multiplexer_1_out));  // open: sel, en
  D_Flip_Flop d_ff_5 (.clk(clock_3_out), .D(out_11), .Q(out_12));  // open: Qn, preset, en, reset
  D_Flip_Flop d_ff_6 (.clk(clock_4_out), .D(d_ff_4_q), .Q(d_ff_6_q));  // open: Qn, preset, en, reset
  D_Flip_Flop d_ff_7 (.clk(clock_1_out), .D(in_4), .Q(out_17));  // open: Qn, preset, en, reset
  D_Flip_Flop d_ff_8 (.clk(clock_2_out), .D(multiplexer_1_out), .Q(d_ff_8_q));  // open: Qn, preset, en, reset
  D_Flip_Flop d_ff_9 (.clk(clock_3_out), .D(out_12), .Q(out_13));  // open: Qn, preset, en, reset
  D_Flip_Flop d_ff_10 (.clk(clock_4_out), .D(d_ff_6_q), .Q(d_ff_10_q));  // open: Qn, preset, en, reset
  Multiplexer multiplexer_2 (.in0(d_ff_8_q), .in1(in_9), .out(multiplexer_2_out));  // open: sel, en
  D_Flip_Flop d_ff_11 (.clk(clock_3_out), .D(out_13), .Q(out_14));  // open: Qn, preset, en, reset
  D_Flip_Flop d_ff_12 (.clk(clock_4_out), .D(d_ff_10_q), .Q(out_15));  // open: Qn, preset, en, reset
  D_Flip_Flop d_ff_13 (.clk(clock_1_out), .D(in_5), .Q(out_18));  // open: Qn, preset, en, reset
  D_Flip_Flop d_ff_14 (.clk(clock_2_out), .D(multiplexer_2_out), .Q(d_ff_14_q));  // open: Qn, preset, en, reset
  Multiplexer multiplexer_3 (.in0(d_ff_14_q), .in1(in_10), .out(multiplexer_3_out));  // open: sel, en
  D_Flip_Flop d_ff_15 (.clk(clock_1_out), .D(in_6), .Q(out_19));  // open: Qn, preset, en, reset
  D_Flip_Flop d_ff_16 (.clk(clock_2_out), .D(multiplexer_3_out), .Q(out_20));  // open: Qn, preset, en, reset

  // Notes on the sheet:
  //   Serial-in to Parallel-out shift register
  //   Serial-in to Serial-out shift register
  //   Parallel-in to Parallel-out shift register
  //   Parallel-in to Serial-out shift register
endmodule
